// Digital circuit 4bits_divisor.dig as structural Verilog
module _4bits_divisor (
  input  [3:0] A,
  input  [3:0] B,
  output [3:0] Q,
  output [3:0] R
);

  wire [3:0] R_out1, R_out2, R_out3;

  divideStep dividestep_1 (.R_in(4'b0000), .A_in(A[3]), .B_in(B), .R_out(R_out1), .Q_out(Q[3]));
  divideStep dividestep_2 (.R_in(R_out1), .A_in(A[2]), .B_in(B), .R_out(R_out2), .Q_out(Q[2]));
  divideStep dividestep_3 (.R_in(R_out2), .A_in(A[1]), .B_in(B), .R_out(R_out3), .Q_out(Q[1]));
  divideStep dividestep_4 (.R_in(R_out3), .A_in(A[0]), .B_in(B), .R_out(R), .Q_out(Q[0]));

  // Other names for the same wires on the sheet: A4 = A[0]; A_in[3:0] = A; A3 = A[1]; A1 = A[3]; B_in[3:0] = B;
  //   Q_out1 = Q[3]; Q_out2 = Q[2]; Q_out3 = Q[1]; Q_out4 = Q[0]; R_out[3:0] = R
endmodule
