// Digital circuit 4bits_multiplier.dig as structural Verilog
module _4bits_multiplier (
  input  [3:0] A,
  input  [3:0] B,
  output [7:0] P
);

  wire C_3A, C_3B, C_4A, C_4B, C_out_1, C_out_2, C_out_3, C_out_4, C_out_5, C_outH_2, C_partial_2a, P01, P02,
       P03, P10, P11, P12, P13, P20, P21, P22, P23, P30, P31, P32, P33, S_3A, S_4A, S_partial_2;

  or or_1 (C_out_4, C_4A, C_4B);
  and and_1 (P[0], A[0], B[0]);
  and and_2 (P10, A[1], B[0]);
  and and_3 (P20, A[2], B[0]);
  and and_4 (P30, A[3], B[0]);
  or or_2 (C_out_3, C_3A, C_3B);
  and and_5 (P01, A[0], B[1]);
  and and_6 (P11, A[1], B[1]);
  and and_7 (P21, A[2], B[1]);
  and and_8 (P31, A[3], B[1]);
  and and_9 (P02, A[0], B[2]);
  and and_10 (P12, A[1], B[2]);
  and and_11 (P22, A[2], B[2]);
  and and_12 (P32, A[3], B[2]);
  or or_3 (C_out_2, C_partial_2a, C_outH_2);
  and and_13 (P03, A[0], B[3]);
  and and_14 (P13, A[1], B[3]);
  and and_15 (P23, A[2], B[3]);
  and and_16 (P33, A[3], B[3]);
  halfadder halfadder_1 (.A(P33), .B(C_out_5), .S(P[6]), .Cout(P[7]));
  halfadder halfadder_2 (.A(S_partial_2), .B(P02), .S(P[2]), .Cout(C_outH_2));
  fullAdder fulladder_1 (.A(P20), .B(P11), .Cin(C_out_1), .S(S_partial_2), .Cout(C_partial_2a));
  fullAdder fulladder_2 (.A(S_3A), .B(P03), .Cin(C_out_2), .S(P[3]), .Cout(C_3B));
  fullAdder fulladder_3 (.A(P30), .B(P21), .Cin(P12), .S(S_3A), .Cout(C_3A));
  halfadder halfadder_3 (.A(S_4A), .B(C_out_3), .S(P[4]), .Cout(C_4B));
  halfadder halfadder_4 (.A(P10), .B(P01), .S(P[1]), .Cout(C_out_1));
  fullAdder fulladder_4 (.A(P32), .B(P23), .Cin(C_out_4), .S(P[5]), .Cout(C_out_5));
  fullAdder fulladder_5 (.A(P31), .B(P22), .Cin(P13), .S(S_4A), .Cout(C_4A));

  // Other names for the same wires on the sheet: C_out_6 = P[7]; P00 = P[0]
endmodule
