// Digital circuit 5bits_adder.dig as structural Verilog
module _5bits_adder (
  input  [4:0] A,
  input  [4:0] B,
  input  Ci,
  output [4:0] S,
  output Co
);

  wire fulladder_1_cout, fulladder_2_cout, fulladder_3_cout, fulladder_4_cout;

  fullAdder fulladder_1 (.A(A[0]), .B(B[0]), .Cin(Ci), .S(S[0]), .Cout(fulladder_1_cout));
  fullAdder fulladder_2 (.A(A[1]), .B(B[1]), .Cin(fulladder_1_cout), .S(S[1]), .Cout(fulladder_2_cout));
  fullAdder fulladder_3 (.A(A[2]), .B(B[2]), .Cin(fulladder_2_cout), .S(S[2]), .Cout(fulladder_3_cout));
  fullAdder fulladder_4 (.A(A[3]), .B(B[3]), .Cin(fulladder_3_cout), .S(S[3]), .Cout(fulladder_4_cout));
  fullAdder fulladder_5 (.A(A[4]), .B(B[4]), .Cin(fulladder_4_cout), .S(S[4]), .Cout(Co));

  // Other names for the same wires on the sheet: Ci_in = Ci; Ci_out = Co
endmodule
