// Digital circuit 8bits_Subtract.dig as structural Verilog
module _8bits_Subtract (
  input  [7:0] A,
  input  [7:0] B,
  output [7:0] SUB
);

  wire [7:0] B_not;

  assign B_not = ~B;  // Not not_1, 8 bits wide
  _8bits_adder _8bits_adder_1 (.A(A), .B(B_not), .Ci(1'b1), .Sum(SUB));  // open: C_out
endmodule
