// Digital circuit 8bits_adder.dig as structural Verilog
module _8bits_adder (
  input  [7:0] A,
  input  [7:0] B,
  input  Ci,
  output [7:0] Sum,
  output C_out
);

  wire C_out_0, C_out_1, C_out_2, C_out_3, C_out_4, C_out_5, C_out_6;

  fullAdder fulladder_1 (.A(A[7]), .B(B[7]), .Cin(C_out_6), .S(Sum[7]), .Cout(C_out));
  fullAdder fulladder_2 (.A(A[6]), .B(B[6]), .Cin(C_out_5), .S(Sum[6]), .Cout(C_out_6));
  fullAdder fulladder_3 (.A(A[5]), .B(B[5]), .Cin(C_out_4), .S(Sum[5]), .Cout(C_out_5));
  fullAdder fulladder_4 (.A(A[4]), .B(B[4]), .Cin(C_out_3), .S(Sum[4]), .Cout(C_out_4));
  fullAdder fulladder_5 (.A(A[3]), .B(B[3]), .Cin(C_out_2), .S(Sum[3]), .Cout(C_out_3));
  fullAdder fulladder_6 (.A(A[2]), .B(B[2]), .Cin(C_out_1), .S(Sum[2]), .Cout(C_out_2));
  fullAdder fulladder_7 (.A(A[1]), .B(B[1]), .Cin(C_out_0), .S(Sum[1]), .Cout(C_out_1));
  fullAdder fulladder_8 (.A(A[0]), .B(B[0]), .Cin(Ci), .S(Sum[0]), .Cout(C_out_0));

  // Other names for the same wires on the sheet: S0 = Sum[0]; S1 = Sum[1]; S2 = Sum[2]; S3 = Sum[3]; S4 = Sum[4];
  //   S5 = Sum[5]; S6 = Sum[6]; S7 = Sum[7]
endmodule
