// Digital circuit 8bits_decrementor.dig as structural Verilog
module _8bits_decrementor (
  input  [7:0] A_in,
  output [7:0] S_out
);

  _8bits_adder _8bits_adder_1 (.A(A_in), .B({8{1'b1}}), .Ci(1'b0), .Sum(S_out));  // open: C_out
endmodule
