// Digital circuit 8bits_incrementor.dig as structural Verilog
module _8bits_incrementor (
  input  [7:0] A_in,
  output [7:0] S_out
);

  _8bits_adder _8bits_adder_1 (.A(A_in), .B(8'h1), .Ci(1'b0), .Sum(S_out));  // open: C_out
endmodule
