// Digital circuit ALU.dig as structural Verilog
module ALU (
  input  [7:0] A_7_0,
  input  [7:0] B_7_0,
  input  [3:0] OP_3_0,
  output [7:0] RES_7_0,
  output Z
);

  wire [7:0] ADD_RES_7_0, Dec_RES_7_0, Div_Res_7_0, Inc_RES_7_0, MUL_RES_7_0, SHL_RES_7_0, SUB_RES_7_0;

  _8bits_Subtract _8bits_subtract_1 (.A(A_7_0), .B(B_7_0), .SUB(SUB_RES_7_0));
  _8bits_adder _8bits_adder_1 (.A(A_7_0), .B(B_7_0), .Ci(1'b0), .Sum(ADD_RES_7_0));  // open: C_out
  _8bits_leftShifter _8bits_leftshifter_1 (.A(A_7_0), .S(SHL_RES_7_0));
  _8bits_incrementor _8bits_incrementor_1 (.A_in(A_7_0), .S_out(Inc_RES_7_0));
  _8bits_decrementor _8bits_decrementor_1 (.A_in(A_7_0), .S_out(Dec_RES_7_0));
  _4bits_divisor _4bits_divisor_1 (.A(A_7_0[3:0]), .B(B_7_0[3:0]), .Q(Div_Res_7_0[7:4]), .R(Div_Res_7_0[3:0]));
  _4bits_multiplier _4bits_multiplier_1 (.A(A_7_0[3:0]), .B(B_7_0[3:0]), .P(MUL_RES_7_0));
  Multiplexer #(.Selector_Bits(4), .Bits(8)) multiplexer_1 (
    .sel(OP_3_0), .in_0(ADD_RES_7_0), .in_1(SUB_RES_7_0), .in_2(B_7_0), .in_3(MUL_RES_7_0),
    .in_4(SHL_RES_7_0), .in_5(Div_Res_7_0), .in_6(Inc_RES_7_0), .in_7(Dec_RES_7_0), .in_8({8{1'b0}}),
    .in_9({8{1'b0}}), .in_10({8{1'b0}}), .in_11({8{1'b0}}), .in_12({8{1'b0}}), .in_13({8{1'b0}}),
    .in_14({8{1'b0}}), .in_15({8{1'b0}}), .out(RES_7_0));
  nor nor_1 (Z, RES_7_0[0], RES_7_0[1], RES_7_0[2], RES_7_0[3], RES_7_0[4], RES_7_0[5], RES_7_0[6], RES_7_0[7]);

  // Other names for the same wires on the sheet: AL_RES_7_0[7:0] = RES_7_0; OP_2_0[3:0] = OP_3_0; Z_out = Z
endmodule
