// Digital circuit DataPath.dig as structural Verilog
module DataPath (
  input  [7:0] WBus_in,
  input  RegA_Ld,
  input  RegB_Ld,
  input  IR_Ld,
  input  [3:0] ULA_Op,
  input  [2:0] WBus_Sel,
  input  CLK,
  input  RST,
  input  [7:0] Mem_Data_in,
  input  [7:0] PC_in,
  output [7:0] WBus_Out,
  output [3:0] OpCode_Out,
  output Z_Flag_Out
);

  wire [3:0] Mux0;
  wire [7:0] Mux2, RegA_out, RegB_out;

  Multiplexer #(.Selector_Bits(3), .Bits(8)) multiplexer_1 (
    .sel(WBus_Sel), .in_0({4'b0000, Mux0}), .in_1(Mem_Data_in), .in_2(Mux2), .in_3(RegA_out),
    .in_4(RegB_out), .in_5(PC_in), .in_6({8{1'b0}}), .in_7({8{1'b0}}), .out(WBus_Out));
  // ULA ula_1: pin names not known; wires that end beside it: RegA_out, RegB_out, ULA_Op, Mux2, Z_Flag_Out
  Register #(.Bits(8)) Reg_A (.D(WBus_in), .C(CLK), .en(RegA_Ld), .Q(RegA_out));
  Register #(.Bits(8)) Reg_B (.D(WBus_in), .C(CLK), .en(RegB_Ld), .Q(RegB_out));
  ResettableRegister resettableregister_1 (
    .D_in(WBus_in), .CLK(CLK), .Ld(IR_Ld), .RST(RST), .Q_out({OpCode_Out, Mux0}));

  // Other names for the same wires on the sheet: Mux1[7:0] = Mem_Data_in; Mux5[7:0] = PC_in; Z_flag = Z_Flag_Out
endmodule
