// Digital circuit divideStep.dig as structural Verilog
module divideStep (
  input  [3:0] R_in,
  input  A_in,
  input  [3:0] B_in,
  output [3:0] R_out,
  output Q_out
);

  wire [3:0] M_in;
  wire [4:4] Sub_out;

  _5bits_Substract _5bits_substract_1 (.A({R_in, A_in}), .B({1'b0, B_in}), .S({Sub_out[4], M_in}));
  not not_1 (Q_out, Sub_out[4]);
  Multiplexer #(.Bits(4)) multiplexer_1 (.sel(Q_out), .in_0({R_in[2:0], A_in}), .in_1(M_in), .out(R_out));

  // Other names for the same wires on the sheet: bp[3:0] = {R_in[2:0], A_in}; P_div[4:0] = {R_in, A_in};
  //   Sub_out[3:0] = M_in
endmodule
