// Digital circuit fullAdder.dig as structural Verilog
module fullAdder (
  input  A,
  input  B,
  input  Cin,
  output S,
  output Cout
);

  wire A_out, B_out, HA1_s;

  halfadder HA1 (.A(A), .B(B), .S(HA1_s), .Cout(A_out));
  or or_1 (Cout, A_out, B_out);
  halfadder HA2 (.A(HA1_s), .B(Cin), .S(S), .Cout(B_out));

  // Other names for the same wires on the sheet: A_in = A; B_in = B; Cin_in = Cin; OR_out = Cout; S_out = S
endmodule
