// Digital circuit halfadder.dig as structural Verilog
module halfadder (
  input  A,
  input  B,
  output S,
  output Cout
);

  xor xor_1 (S, A, B);
  and and_1 (Cout, A, B);

  // Other names for the same wires on the sheet: AND_out = Cout; XOR_out = S
endmodule
