// Digital circuit newCPU.dig as structural Verilog
module newCPU (
  input  CLK,
  input  RST
);

  wire CPU_CLK, HLT, IR_ld, MAR_ld, not_1_out, OUT_ld, PC_en, PC_ld, RegA_ld, RegB_ld, Z_Flag;
  wire [2:0] WBus_sel;
  wire [3:0] OpCode, OUT_Reg_q_out, OUT_Reg_q_out_2, ULA_op;
  wire [7:0] MEM_data, PC_out, W_bus;

  memory memory_1 (.WBus_in(W_bus), .MAR_LD(MAR_ld), .CLK(CPU_CLK), .RST(RST), .Data_Out(MEM_data));
  ControlUnit controlunit_1 (
    .OpCode_in(OpCode), .ZFlag_in(Z_Flag), .CLK(CPU_CLK), .RST(RST), .WBus_Sel(WBus_sel), .PC_en(PC_en),
    .PC_ld(PC_ld), .MAR_ld(MAR_ld), .IR_ld(IR_ld), .RegA_ld(RegA_ld), .RegB_ld(RegB_ld), .OUT_ld(OUT_ld),
    .ULA_op(ULA_op), .HLT(HLT));
  ResettableRegister OUT_Reg (
    .D_in(W_bus), .CLK(CPU_CLK), .Ld(OUT_ld), .RST(RST), .Q_out({OUT_Reg_q_out_2, OUT_Reg_q_out}));
  Seven_Seg_Hex seven_seg_hex_1 (.d(OUT_Reg_q_out_2), .dp(1'b0));
  newPC newpc_1 (.WBus_in(W_bus), .PC_en(PC_en), .PC_ld(PC_ld), .CLK(CPU_CLK), .RST(RST), .PC_Out(PC_out));
  DataPath datapath_1 (
    .WBus_in(W_bus), .RegA_Ld(RegA_ld), .RegB_Ld(RegB_ld), .IR_Ld(IR_ld), .ULA_Op(ULA_op),
    .WBus_Sel(WBus_sel), .CLK(CPU_CLK), .RST(RST), .Mem_Data_in(MEM_data), .PC_in(PC_out), .WBus_Out(W_bus),
    .OpCode_Out(OpCode), .Z_Flag_Out(Z_Flag));
  Seven_Seg_Hex seven_seg_hex_2 (.d(OUT_Reg_q_out), .dp(1'b0));
  not not_1 (not_1_out, HLT);
  and and_1 (CPU_CLK, not_1_out, CLK);

  // Notes on the sheet:
  //   CLK: Hz: 3
endmodule
